// Logisim project Conversor_7_segmentos.circ as structural Verilog: 8 circuits, main circuit Conversor 
module Conversor (
  input  E2,
  input  E1,
  input  E0,
  output out_4,
  output out_5,
  output out_6,
  output out_7,
  output out_8,
  output out_9,
  output out_10
);

  A a_1 (.E2(E2), .E1(E1), .E0(E0), .out_4(out_4));
  B b_1 (.E2(E2), .E1(E1), .E0(E0), .out_4(out_5));
  C c_1 (.E2(E2), .E1(E1), .E0(E0), .out_4(out_6));
  D d_1 (.E2(E2), .E1(E1), .E0(E0), .out_4(out_7));
  E e_1 (.E2(E2), .E1(E1), .E0(E0), .out_4(out_8));
  F f_1 (.E2(E2), .E1(E1), .E0(E0), .out_4(out_9));
  G g_1 (.E2(E2), .E1(E1), .E0(E0), .out_4(out_10));
endmodule

module A (
  input  E2,
  input  E1,
  input  E0,
  output out_4
);

  wire and_1_out, and_2_out, and_3_out, not_1_out, not_2_out, not_3_out;

  not not_1 (not_1_out, E2);
  not not_2 (not_2_out, E1);
  not not_3 (not_3_out, E0);
  and and_1 (and_1_out, not_1_out, E1);
  and and_2 (and_2_out, E2, not_2_out);
  and and_3 (and_3_out, E2, not_3_out);
  or or_1 (out_4, and_1_out, and_2_out, and_3_out);
endmodule

module B (
  input  E2,
  input  E1,
  input  E0,
  output out_4
);

  wire and_1_out, and_2_out, and_3_out, not_1_out, not_2_out;

  not not_1 (not_1_out, E1);
  not not_2 (not_2_out, E0);
  and and_1 (and_1_out, E2, not_2_out);
  and and_2 (and_2_out, E2, not_1_out);
  and and_3 (and_3_out, not_1_out, not_2_out);
  or or_1 (out_4, and_1_out, and_2_out, and_3_out);
endmodule

module C (
  input  E2,
  input  E1,
  input  E0,
  output out_4
);

  wire and_1_out, and_2_out, not_1_out, not_2_out;

  not not_1 (not_1_out, E2);
  not not_2 (not_2_out, E0);
  and and_1 (and_1_out, not_1_out, not_2_out);
  and and_2 (and_2_out, E2, E0);
  or or_1 (out_4, and_1_out, E1, and_2_out);
endmodule

module D (
  input  E2,
  input  E1,
  input  E0,
  output out_4
);

  wire and_1_out, and_2_out, not_1_out, not_2_out, not_3_out;

  not not_1 (not_1_out, E1);
  not not_2 (not_2_out, E0);
  and and_1 (and_1_out, E1, E0);
  not not_3 (not_3_out, E2);
  and and_2 (and_2_out, not_1_out, not_1_out, not_2_out);
  or or_1 (out_4, and_1_out, not_3_out, and_2_out);
endmodule

module E (
  input  E2,
  input  E1,
  input  E0,
  output out_4
);

  wire and_1_out, and_2_out, not_1_out, not_2_out;

  not not_1 (not_1_out, E2);
  not not_2 (not_2_out, E0);
  and and_1 (and_1_out, not_1_out, not_2_out);
  and and_2 (and_2_out, E1, not_2_out);
  or or_1 (out_4, and_1_out, and_2_out);
endmodule

module F (
  input  E2,
  input  E1,
  input  E0,
  output out_4
);

  wire and_1_out, and_2_out, and_3_out, and_4_out, not_1_out, not_2_out, not_3_out;

  not not_1 (not_1_out, E2);
  not not_2 (not_2_out, E0);
  not not_3 (not_3_out, E1);
  and and_1 (and_1_out, not_1_out, not_2_out);
  and and_2 (and_2_out, E1, not_2_out);
  and and_3 (and_3_out, not_1_out, E1);
  and and_4 (and_4_out, not_3_out, E2, E0);
  or or_1 (out_4, and_1_out, and_2_out, and_3_out, and_4_out);
endmodule

module G (
  input  E2,
  input  E1,
  input  E0,
  output out_4
);

  wire not_1_out;

  not not_1 (not_1_out, E1);
  or or_1 (out_4, E2, not_1_out, E0);
endmodule
