// Logisim project ExerLogisim.circ as structural Verilog: 1 circuit, main circuit main
module main (
  input  A0,
  input  A1,
  input  A2,
  input  B0,
  input  B1,
  input  B2
);

  wire clock_1_out, conversor_1_out_4, conversor_1_out_5, conversor_1_out_6, conversor_1_out_7,
       conversor_1_out_8, conversor_1_out_9, conversor_1_out_10, registrador_de_3_bits_1_out_5,
       registrador_de_3_bits_1_out_6, registrador_de_3_bits_1_out_7, somador_de_3_bits_1_s0,
       somador_de_3_bits_1_s1, somador_de_3_bits_1_s2;

  Somador_de_3_bits somador_de_3_bits_1 (
    .A0(A0), .B0(B0), .S0(somador_de_3_bits_1_s0), .A1(A1), .B1(B1), .S1(somador_de_3_bits_1_s1),
    .S2(somador_de_3_bits_1_s2), .A2(A2), .B2(B2));  // open: C
  Registrador_de_3_bits registrador_de_3_bits_1 (
    .in_2(somador_de_3_bits_1_s2), .in_3(somador_de_3_bits_1_s1), .in_4(somador_de_3_bits_1_s0),
    .out_5(registrador_de_3_bits_1_out_5), .out_6(registrador_de_3_bits_1_out_6),
    .out_7(registrador_de_3_bits_1_out_7), .CLK(clock_1_out));
  Clock clock_1 (.out(clock_1_out));
  Conversor conversor_1 (
    .E2(registrador_de_3_bits_1_out_5), .E1(registrador_de_3_bits_1_out_6),
    .E0(registrador_de_3_bits_1_out_7), .out_4(conversor_1_out_4), .out_5(conversor_1_out_5),
    .out_6(conversor_1_out_6), .out_7(conversor_1_out_7), .out_8(conversor_1_out_8),
    .out_9(conversor_1_out_9), .out_10(conversor_1_out_10));
  _7_Segment_Display u_7_segment_display_1 (
    .g(conversor_1_out_4), .f(conversor_1_out_5), .a(conversor_1_out_6), .b(conversor_1_out_7),
    .e(conversor_1_out_8), .d(conversor_1_out_9), .c(conversor_1_out_10));  // open: dp

  // Notes on the sheet:
  //   Somador 3 bits
  //   Registrador 3 bits
endmodule
