// Logisim project Registrador.circ as structural Verilog: 1 circuit, main circuit Registrador de 3 bits
module Registrador_de_3_bits (
  input  CLK,
  input  in_2,
  input  in_3,
  input  in_4,
  output out_5,
  output out_6,
  output out_7
);

  D_Flip_Flop d_ff_1 (.clk(CLK), .D(in_2), .Q(out_5));  // open: Qn, preset, en, reset
  D_Flip_Flop d_ff_2 (.clk(CLK), .D(in_3), .Q(out_6));  // open: Qn, preset, en, reset
  D_Flip_Flop d_ff_3 (.clk(CLK), .D(in_4), .Q(out_7));  // open: Qn, preset, en, reset
endmodule
