// Logisim project Somador de 3 bits.circ as structural Verilog: 3 circuits, main circuit Somador de 3 bits
module Somador_de_3_bits (
  input  A0,
  input  B0,
  input  A1,
  input  B1,
  input  A2,
  input  B2,
  output S0,
  output S1,
  output S2,
  output C
);

  wire fa_1_co, ha_1_c;

  HA ha_1 (.A(A0), .B(B0), .S(S0), .C(ha_1_c));
  FA fa_1 (.A(A1), .B(B1), .CI(ha_1_c), .S(S1), .CO(fa_1_co));
  FA fa_2 (.A(A2), .B(B2), .CI(fa_1_co), .S(S2), .CO(C));
endmodule

module HA (
  input  A,
  input  B,
  output S,
  output C
);

  xor xor_1 (S, A, B);
  and and_1 (C, A, B);
endmodule

module FA (
  input  A,
  input  B,
  input  CI,
  output S,
  output CO
);

  wire and_1_out, and_2_out, xor_1_out;

  xor xor_1 (xor_1_out, A, B);
  xor xor_2 (S, xor_1_out, CI);
  and and_1 (and_1_out, xor_1_out, CI);
  and and_2 (and_2_out, B, A);
  or or_1 (CO, and_1_out, and_2_out);
endmodule
