// Logisim project conversor de 7 segementos.circ as structural Verilog: 8 circuits, main circuit D
module D (
  input  I1,
  input  I2,
  input  I3,
  output D
);

  wire and_1_out, and_2_out, not_1_out, not_2_out, not_3_out;

  not not_1 (not_1_out, I1);
  not not_2 (not_2_out, I2);
  not not_3 (not_3_out, I3);
  and and_1 (and_1_out, I2, I3);
  and and_2 (and_2_out, not_2_out, not_3_out);
  or or_1 (D, not_1_out, and_1_out, and_2_out);
endmodule

module A (
  input  I1,
  input  I2,
  input  I3,
  output A
);

  wire and_1_out, and_2_out, and_3_out, not_1_out, not_2_out, not_3_out, or_1_out;

  not not_1 (not_1_out, I1);
  not not_2 (not_2_out, I2);
  not not_3 (not_3_out, I3);
  and and_1 (and_1_out, not_1_out, I2);
  and and_2 (and_2_out, I1, not_2_out);
  and and_3 (and_3_out, I2, not_3_out);
  or or_1 (or_1_out, and_1_out, and_2_out);
  or or_2 (A, or_1_out, and_3_out);
endmodule

module B (
  input  I,
  input  I2,
  input  I3,
  output B
);

  wire and_1_out, and_2_out, and_3_out, not_1_out, not_2_out, not_3_out, not_4_out;

  not not_1 (not_1_out, I3);
  not not_2 (not_2_out, I2);
  not not_3 (not_3_out, I3);
  not not_4 (not_4_out, I2);
  and and_1 (and_1_out, I, not_1_out);
  and and_2 (and_2_out, not_2_out, not_3_out);
  and and_3 (and_3_out, I, not_4_out);
  or or_1 (B, and_1_out, and_2_out, and_3_out);
endmodule

module C (
  input  I1,
  input  I2,
  input  I3,
  output C
);

  wire and_1_out, and_2_out, not_1_out, not_2_out;

  not not_1 (not_1_out, I1);
  not not_2 (not_2_out, I3);
  and and_1 (and_1_out, not_1_out, not_2_out);
  and and_2 (and_2_out, I1, I3);
  or or_1 (C, and_1_out, I2, and_2_out);
endmodule

module E (
  input  I1,
  input  I2,
  input  I3,
  output E
);

  wire and_1_out, and_2_out, not_1_out, not_2_out, not_3_out;

  not not_1 (not_1_out, I1);
  not not_2 (not_2_out, I3);
  not not_3 (not_3_out, I3);
  and and_1 (and_1_out, not_1_out, not_2_out);
  and and_2 (and_2_out, I2, not_3_out);
  or or_1 (E, and_1_out, and_2_out);
endmodule

module F (
  input  I1,
  input  I2,
  input  I3,
  output F
);

  wire and_1_out, and_2_out, and_3_out, and_4_out, not_1_out, not_2_out, not_3_out, not_4_out, not_5_out;

  not not_1 (not_1_out, I1);
  not not_2 (not_2_out, I3);
  not not_3 (not_3_out, I3);
  not not_4 (not_4_out, I1);
  not not_5 (not_5_out, I2);
  and and_1 (and_1_out, not_1_out, not_2_out);
  and and_2 (and_2_out, I2, not_3_out);
  and and_3 (and_3_out, not_4_out, I2);
  and and_4 (and_4_out, I1, not_5_out, I3);
  or or_1 (F, and_1_out, and_2_out, and_3_out, and_4_out);
endmodule

module G (
  input  I1,
  input  I2,
  input  I3,
  output G
);

  wire not_1_out;

  not not_1 (not_1_out, I2);
  or or_1 (G, I1, not_1_out, I3);
endmodule

module Principal (
  input  E2,
  input  E1,
  input  E0,
  output A,
  output B,
  output out_6,
  output out_7,
  output out_8,
  output out_9,
  output out_10
);

  A u_A (.I1(E2), .I2(E1), .I3(E0), .A(A));
  B u_B (.I(E2), .I2(E1), .I3(E0), .B(B));
  C C (.I1(E2), .I2(E1), .I3(E0), .C(out_6));
  D D (.I1(E2), .I2(E1), .I3(E0), .D(out_7));
  E E (.I1(E2), .I2(E1), .I3(E0), .E(out_8));
  F F (.I1(E2), .I2(E1), .I3(E0), .F(out_9));
  G G (.I1(E2), .I2(E1), .I3(E0), .G(out_10));
endmodule
